// Logisim project lab1-adder.circ as structural Verilog: 3 circuits, main circuit four_bit_adder
module main (
  input  A,
  input  B,
  output A_XOR_B
);

  wire and_1_out, and_2_out, not_1_out, not_2_out;

  not not_1 (not_1_out, A);
  not not_2 (not_2_out, B);
  and and_1 (and_1_out, not_1_out, B);
  and and_2 (and_2_out, A, not_2_out);
  or or_1 (A_XOR_B, and_1_out, and_2_out);

  // Notes on the sheet:
  //   XOR circuit built using Logisim
endmodule

module one_bit_adder (
  input  A,
  input  B,
  input  Cin,
  output S,
  output Cout
);

  wire and_1_out, and_2_out, xor_1_out;

  xor xor_1 (xor_1_out, A, B);
  and and_1 (and_1_out, xor_1_out, Cin);
  and and_2 (and_2_out, A, B);
  xor xor_2 (S, xor_1_out, Cin);
  or or_1 (Cout, and_1_out, and_2_out);

  // Notes on the sheet:
  //   1-bit adder
endmodule

module four_bit_adder (
  input  [3:0] A4,
  input  [3:0] B4,
  input  Cin,
  output Cout,
  output [3:0] S4
);

  wire one_bit_adder_1_cout, one_bit_adder_2_cout, one_bit_adder_3_cout;

  one_bit_adder one_bit_adder_1 (.A(A4[0]), .B(B4[0]), .Cin(Cin), .S(S4[0]), .Cout(one_bit_adder_1_cout));
  one_bit_adder one_bit_adder_2 (
    .A(A4[1]), .B(B4[1]), .Cin(one_bit_adder_1_cout), .S(S4[1]), .Cout(one_bit_adder_2_cout));
  one_bit_adder one_bit_adder_3 (
    .A(A4[2]), .B(B4[2]), .Cin(one_bit_adder_2_cout), .S(S4[2]), .Cout(one_bit_adder_3_cout));
  one_bit_adder one_bit_adder_4 (.A(A4[3]), .B(B4[3]), .Cin(one_bit_adder_3_cout), .S(S4[3]), .Cout(Cout));
endmodule
